# Fritzing sketch machdien (saved by Fritzing 0.9.3b)
breadboards: 1

parts:
  Adafruit_HUZZAH_ESP8266_Breakout1 = Adafruit HUZZAH ESP8266 Breakout [part_number=2471]
  LED1 = smd LED [color="Red (633nm)" package="0603 [SMD]"]
  LED2 = smd LED [color="Red (633nm)" package="0603 [SMD]"]
  RHT1 = Humidity and Temperature Sensor RHT03
  R1 = PHOTOCELL [package=photocell]

nets:
  N1: Adafruit_HUZZAH_ESP8266_Breakout1.#12, R1.P$1
  N2: Adafruit_HUZZAH_ESP8266_Breakout1.#14, RHT1.Data-signal
  N3: Adafruit_HUZZAH_ESP8266_Breakout1.#5, LED2.anode
  N4: Adafruit_HUZZAH_ESP8266_Breakout1.#4, LED1.anode
  N5: Adafruit_HUZZAH_ESP8266_Breakout1.3V, RHT1.Vcc
  N6: Adafruit_HUZZAH_ESP8266_Breakout1.GND, LED1.cathode, LED2.cathode, RHT1.GND_2, R1.P$2
